# Fritzing sketch Untitled Sketch (saved by Fritzing 0.7.1b)
breadboards: 1

parts:
  C1 = Electrolytic Capacitor [capacitance=1µF package="100 mil [THT, electrolytic]"]
  Arduino1 = Arduino

nets:
  N1: C1.-, Arduino1.GND
  N2: C1.+, Arduino1.+5V
